# Fritzing sketch IOT (saved by Fritzing 0.9.6b)
breadboards: 1

parts:
  U2 = 2-Channel 5v Relay Shield [package=relay-2ch5v10a]
  IC1 = Voltage Regulator [package=78xxl]
  R1 = Resistor [tolerance=±5% power=0.25 resistance=2.2k package=THT]
  R2 = Resistor [tolerance=±5% resistance=220 package="0402 [SMD]"]
  Q4 = NPN-Transistor [package="TO92 [THT]"]
  R3 = Resistor [tolerance=±5% power=0.25 resistance=2.2k package=THT]
  R4 = Resistor [tolerance=±5% resistance=220 package="0402 [SMD]"]
  Q5 = NPN-Transistor [package="TO92 [THT]"]
  U3 = ESP8266 NodeMCU LoLin module
  M1 = gear-motor
  M2 = gear-motor
  VCC1 = Battery
  VCC2 = Battery

nets:
  VCC: U2.VCC, IC1.OUT, R2.Pin_0, R4.Pin_0, U3.Vin
  GND: U2.GND, U2.K1-In, U2.K2-In, IC1.GND, Q4.E, Q5.E, U3.GND, VCC1.-, VCC2.-
  N1: U2.IN1, Q4.C
  N2: U2.IN2, R2.Pin_1, Q5.C
  N3: U2.K1-On, M2.pin_2
  N4: U2.K2-On, M1.pin_2
  N5: IC1.IN, VCC1.+, VCC2.+
  N6: R1.Pin_0, U3.D1
  N7: R1.Pin_1, Q5.B
  N8: Q4.B, R3.Pin_1
  N9: R3.Pin_0, U3.D0
  N10: M1.pin_1, M2.pin_1

custom parts:
  2-Channel 5v Relay Shield: 2 Channel 5v Relay Shield w. 2x SPD-06VDC-SD-C
  ESP8266 NodeMCU LoLin module: ESP8266 based NodeMCU
